# Fritzing sketch Untitled Sketch 2 (saved by Fritzing 0.9.3b)

parts:
  HC-SR04_Sensor_1 = HC-SR04 Ultrasonic Distance Sensor
  U1 = LuaNode32 / ESP32
  U3 = Vibration Motor- ROB-08449 [package=vibe-motor-10mm]

nets:
  VCC: HC-SR04_Sensor_1.VCC, U1.Vin
  N1: HC-SR04_Sensor_1.TRIG, U1.D2
  N2: HC-SR04_Sensor_1.ECHO, U1.D5
  GND: HC-SR04_Sensor_1.GND, U1.GND
  N3: U1.D22, U3.+
  N4: U1.D23, U3.-

custom parts:
  LuaNode32 / ESP32: ESP32 based LuaNode32
